# Fritzing sketch zeppelin (saved by Fritzing 1.0.4)
breadboards: 1

parts:
  R1 = Resistor [tolerance=±5% power=0.25W resistance=470 package=THT]
  R2 = Resistor [tolerance=±5% power=0.25W resistance=470 package=THT]
  R3 = Resistor [tolerance=±5% power=0.25W resistance=470 package=THT]
  R4 = Resistor [tolerance=±5% power=0.25W resistance=470 package=THT]
  R5 = Resistor [tolerance=±5% power=0.25W resistance=470 package=THT]
  R6 = Resistor [tolerance=±5% power=0.25W resistance=470 package=THT]
  LED1 = LED - 3mm [color="Red (633nm)" current=0.030A package="3 mm [THT]"]
  LED2 = LED - 3mm [color="Green (570nm)" current=0.030A package="3 mm [THT]"]
  LED3 = LED - 3mm [color="Green (570nm)" current=0.030A package="3 mm [THT]"]
  LED4 = LED - 3mm [color="Green (570nm)" current=0.030A package="3 mm [THT]"]
  LED5 = LED - 3mm [color="Red (633nm)" current=0.030A package="3 mm [THT]"]
  LED6 = LED - 3mm [color="Green (570nm)" current=0.030A package="3 mm [THT]"]
  Nano1 = Arduino Nano v2.3
  S1 = SWITCH-MOMENTARY-2 [package=reed_switch_pth]
  S2 = SWITCH-MOMENTARY-2 [package=reed_switch_pth]
  L1 = Solenoid [part_number=Electromagnet]
  Q1 = Basic FET N-Channel [part_number=IRLZ44N package="TO220 [THT]"]
  R7 = Resistor [tolerance=±5% power=0.25W resistance=220 package=THT]
  R8 = Resistor [tolerance=±5% power=0.25W resistance=10k package=THT]
  D1 = Rectifier Diode [part_number=1N4001 package="Melf DO-213 AB [SMD]"]
  R9 = Resistor [tolerance=±5% power=0.25W resistance=220 package=THT]
  R10 = Resistor [tolerance=±5% power=0.25W resistance=10k package=THT]
  L2 = Solenoid [part_number=Electromagnet]
  Q2 = Basic FET N-Channel [part_number=IRLZ44N package="TO220 [THT]"]
  D2 = Rectifier Diode [part_number=1N4001 package="Melf DO-213 AB [SMD]"]
  J2 = Power Jack [package=power_jack_combo]  # not connected
  J3 = Screw terminal - 2 pins [package=THT]  # not connected
  Start = SWITCH-MOMENTARY-2 [package=reed_switch_pth]
  Reset = SWITCH-MOMENTARY-2 [package=reed_switch_pth]

nets:
  Figure8LedRed: R1.Pin_0, Nano1.D12
  N1: R1.Pin_1, LED1.anode
  Figure8LedGreen1: R2.Pin_0, Nano1.D11
  N2: R2.Pin_1, LED2.anode
  Figure8LedGreen2: R3.Pin_0, Nano1.D10
  N3: R3.Pin_1, LED3.anode
  Figure8LedGreen3: R4.Pin_0, Nano1.D9
  N4: R4.Pin_1, LED4.anode
  ShuttleLedRed: R5.Pin_0, Nano1.D6
  N5: R5.Pin_1, LED5.anode
  ShuttleLedGreen: R6.Pin_0, Nano1.D5
  N6: R6.Pin_1, LED6.anode
  GND: LED1.cathode, LED2.cathode, LED3.cathode, LED4.cathode, LED5.cathode, LED6.cathode, Nano1.GND, S1.2, S2.2, Q1.source, R8.Pin_1, R10.Pin_1, Q2.source, Start.2, Reset.1
  N7: Nano1.RST, Reset.2
  N8: Nano1.D2, Start.1
  ShuttleReedSwitch: Nano1.D3, S2.1
  ShuttleMagnet: Nano1.D4, R9.Pin_0, R10.Pin_0
  Figure8ReedSwitch: Nano1.D7, S1.1
  Figure8Magnet: Nano1.D8, R7.Pin_0, R8.Pin_0
  5V: Nano1.VIN, L1.pin1, D1.cathode, L2.pin1, D2.cathode
  N9: L1.pin2, Q1.drain, D1.anode
  N10: Q1.gate, R7.Pin_1
  N11: R9.Pin_1, Q2.gate
  N12: L2.pin2, Q2.drain, D2.anode
